# Fritzing sketch RecyclingChallenge (saved by Fritzing 0.9.3b)
breadboards: 1

parts:
  A1 = Arduino UNO R4 WiFi
  12V = Power plug
  RFID_Reader = RFID-RC522-v2
  Επαγωγικός_Αισθητήρας = LJ18A3-H-ZBX [part_number=LJ18A3-8-Z/BX package=THT]
  Load_Cell = Load Cell - Red/white/black/green [part_number="Αισθητήρας Βάρους"]
  Εξάρτημα2 = HX711 Weighing Sensor Module [part_number="Ενισχυτής Αισθητήρα Βάρους"]
  Εξάρτημα3 = LCD1602-I2C [part_number="Οθόνη LCD"]
  A2 = laser emitter [part_number=Laser]
  R1 = PHOTOCELL [part_number=Photoresistor package=photocell]
  R2 = Resistor [tolerance=±5% resistance=1k package=THT]
  R3 = Resistor [tolerance=±5% resistance=100 package=THT]
  J1 = Piezo Speaker [part_number=Buzzer]

nets:
  GND: A1.Pin_2, A1.Pin_9, A1.Pin_18, 12V.GND, RFID_Reader.GND, Επαγωγικός_Αισθητήρας.VO_(BLU), Εξάρτημα2.GND, Εξάρτημα3.GND, A2.Pin_2, R2.Pin_1, R3.Pin_0
  N1: A1.Pin_7, RFID_Reader.3.3V
  VCC: A1.Pin_8, Εξάρτημα2.VCC, Εξάρτημα3.VCC, R1.P$2
  N2: A1.Pin_12, R1.P$1, R2.Pin_0
  N3: A1.Pin_36, Εξάρτημα2.DO/RX
  N4: A1.Pin_37, Εξάρτημα2.CK/TX
  N5: A1.Pin_39, RFID_Reader.RST
  N6: A1.Pin_40, J1.pin2
  N7: A1.Pin_41, A2.Pin_1
  N8: A1.Pin_42, Επαγωγικός_Αισθητήρας.SIG_(BLK)
  N9: A1.Pin_44, RFID_Reader.SDA
  N10: A1.Pin_45, RFID_Reader.MOSI
  N11: A1.Pin_46, RFID_Reader.MISO
  N12: A1.Pin_47, RFID_Reader.SCK
  N13: A1.Pin_50, Εξάρτημα3.SDA
  N14: A1.Pin_51, Εξάρτημα3.SCL
  N15: 12V.VCC, Επαγωγικός_Αισθητήρας.VI_(BRN)
  N16: Load_Cell.wire1, Εξάρτημα2.E+
  N17: Load_Cell.wire2, Εξάρτημα2.A+
  N18: Load_Cell.wire3, Εξάρτημα2.E-
  N19: Load_Cell.wire4, Εξάρτημα2.A-
  N20: R3.Pin_1, J1.pin1

custom parts:
  Arduino UNO R4 WiFi: The Arduino UNO R4 WiFi merges the RA4M1 microprocessor from Renesas with the ESP32-S3 from Espressif, creating an all-in-one tool for makers with enhanced processing power and a diverse array of new peripherals.
  RFID-RC522-v2: A simple China made RFID-RC522 Reader; do check the pin labels, as this is a MFRC522 based clone.
  LJ18A3-H-ZBX: LJ18A3-H-ZBX Proximity Sensor module.
  Load Cell - Red/white/black/green: A rectangle load cell/weighting pressure Sensor with four wires - Red, white, black, green. Normally corresponding with E+, E-, A+, A- respectively.
  HX711 Weighing Sensor Module: HX711 is a precision 24-bit analog-to-digital converter (ADC) designed for weigh scales and industrial control applications to interface directly with a bridge sensor.
  LCD1602-I2C: A standard character display, usually with 2x16 characters. Comes in many colors with LCM1602 IIC attached.
  laser emitter: Laser Diode 650nm 5mW 2.8V ~ 5.2V 25mA Cylinder (10mm Dia).
